// Logisim project P3_V2.circ as structural Verilog: 7 circuits, main circuit main
module main (
  input  in_1,
  input  in_2,
  input  in_3,
  input  [15:0] in_4
);

  wire CLK, controlunit_1_regwrite, SelReadReg;
  wire [1:0] rom_1_data, SignalALU;
  wire [2:0] ArgA, ArgB, RD;
  wire [10:0] Immediate;
  wire [15:0] adder_1_out, PC_q, registerfile_1_rd, registerfile_1_readdata1, registerfile_1_readdata2,
       registerfile_1_readdata3, registerfile_1_readdata4, Result;

  Register #(.width(16)) PC (.D(adder_1_out), .en(in_2), .clk(CLK), .Q(PC_q));  // open: clr
  Clock u_CLK (.out(CLK));
  ROM #(.addrWidth(16), .dataWidth(16)) rom_1 (.addr(PC_q), .data({Immediate, RD, rom_1_data}));
  Adder #(.width(16)) adder_1 (.a(PC_q), .b(in_4), .out(adder_1_out), .cin(in_3));  // open: cout
  Multiplexer #(.width(3)) multiplexer_1 (.in0(RD), .in1(Immediate[2:0]), .out(ArgA), .sel(SelReadReg));
  Multiplexer #(.width(3)) multiplexer_2 (.in0(Immediate[2:0]), .in1(Immediate[5:3]), .out(ArgB), .sel(SelReadReg));
  ControlUnit controlunit_1 (
    .RG(in_1), .Opcode(rom_1_data), .RegWrite(controlunit_1_regwrite), .SelReadReg1(SelReadReg),
    .SignalALU(SignalALU));
  RegisterFile registerfile_1 (
    .RegWrite(controlunit_1_regwrite), .WriteRegister(RD), .ReadRegister1(ArgA), .ReadRegister2(ArgB),
    .WriteData(Result), .Clock(CLK), .ReadData1(registerfile_1_readdata1),
    .ReadData2(registerfile_1_readdata2), .ReadData3(registerfile_1_readdata3),
    .ReadData4(registerfile_1_readdata4), .RD(registerfile_1_rd));
  ALU alu_1 (
    .ArgA(registerfile_1_readdata1), .ArgB(registerfile_1_readdata2), .ArgC(registerfile_1_readdata3),
    .ArgD(registerfile_1_readdata4), .RD(registerfile_1_rd), .Immediate(Immediate), .SignalALU(SignalALU),
    .Result(Result));

  // Notes on the sheet:
  //   in_2: initial=0x1
  //   in_4: initial=0x1
  //   in_1: initial=0x1
  //   contents of rom_1 (hex, n*v repeats v):
  //   40 64 88 4c 30 b4 58 5c 2d 42 683
  //   RS1
  //   RS2
endmodule

module ControlUnit (
  input  RG,
  input  [1:0] Opcode,
  output RegWrite,
  output SelReadReg1,
  output [1:0] SignalALU
);

  and and_1 (SelReadReg1, Opcode[0], Opcode[1]);

  assign RegWrite = RG;
  assign SignalALU = Opcode;

  // Notes on the sheet:
  //   RG: initial=0x1
endmodule

module dot (
  input  [15:0] ArgA,
  input  [15:0] ArgB,
  input  [15:0] ArgC,
  input  in_4,
  input  [15:0] ArgD,
  output [15:0] Result
);

  wire [15:0] multiplier_1_out, multiplier_2_out;

  Multiplier #(.width(16)) multiplier_1 (.a(ArgA), .b(ArgB), .out(multiplier_1_out));  // open: cin, cout
  Multiplier #(.width(16)) multiplier_2 (.a(ArgC), .b(ArgD), .out(multiplier_2_out));  // open: cin, cout
  Adder #(.width(16)) adder_1 (.a(multiplier_1_out), .b(multiplier_2_out), .out(Result), .cin(in_4));  // open: cout
endmodule

module add (
  input  [15:0] ArgA,
  input  in_2,
  input  [15:0] ArgB,
  output [15:0] Result
);

  Adder #(.width(16)) adder_1 (.a(ArgA), .b(ArgB), .out(Result), .cin(in_2));  // open: cout
endmodule

module li (
  input  [10:0] Immediate,
  output [15:0] Result
);

  assign Result = {{5{Immediate[10]}}, Immediate};  // Bit_Extender bit_extender_1
endmodule

module ALU (
  input  [15:0] ArgA,
  input  [15:0] ArgB,
  input  [15:0] ArgC,
  input  [15:0] ArgD,
  input  [15:0] RD,
  input  [10:0] Immediate,
  input  [1:0] SignalALU,
  output [15:0] Result
);

  wire [15:0] add_1_result, add_2_result, dot_1_result, LiResult;

  add add_1 (.ArgA(ArgA), .ArgB(ArgB), .Result(add_1_result));  // open: in_2
  dot dot_1 (.ArgA(ArgA), .ArgB(ArgB), .ArgC(ArgC), .ArgD(ArgD), .Result(dot_1_result));  // open: in_4
  li li_1 (.Immediate(Immediate), .Result(LiResult));
  add add_2 (.ArgA(dot_1_result), .ArgB(RD), .Result(add_2_result));  // open: in_2
  Multiplexer #(.select(2), .width(16)) multiplexer_1 (
    .in0(LiResult), .in1(add_1_result), .in2(dot_1_result), .in3(add_2_result), .out(Result), .sel(SignalALU));
endmodule

module RegisterFile (
  input  RegWrite,
  input  [2:0] WriteRegister,
  input  [2:0] ReadRegister1,
  input  [2:0] ReadRegister2,
  input  [15:0] WriteData,
  input  Clock,
  output [15:0] ReadData1,
  output [15:0] ReadData2,
  output [15:0] ReadData3,
  output [15:0] ReadData4,
  output [15:0] RD
);

  wire EN_R0, EN_R1, EN_R2, EN_R3, EN_R4, EN_R5, EN_R6, EN_R7;
  wire [2:0] ACC, adder_1_out, adder_2_out;
  wire [15:0] OutR0, OutR1, OutR2, OutR3, OutR4, OutR5, OutR6, OutR7;

  assign ACC = {{2{1'b0}}, RegWrite};  // Bit_Extender bit_extender_1
  Demultiplexer #(.select(3)) demultiplexer_1 (
    .out0(EN_R0), .out1(EN_R1), .out2(EN_R2), .out3(EN_R3), .out4(EN_R4), .out5(EN_R5), .out6(EN_R6),
    .out7(EN_R7), .in(RegWrite), .sel(WriteRegister));
  Multiplexer #(.select(3), .width(16)) multiplexer_1 (
    .in0(OutR0), .in1(OutR1), .in2(OutR2), .in3(OutR3), .in4(OutR4), .in5(OutR5), .in6(OutR6), .in7(OutR7),
    .out(ReadData1), .sel(ReadRegister1));
  Adder #(.width(3)) adder_1 (.a(ReadRegister1), .b(ACC), .out(adder_1_out));  // open: cin, cout
  Multiplexer #(.select(3), .width(16)) multiplexer_2 (
    .in0(OutR0), .in1(OutR1), .in2(OutR2), .in3(OutR3), .in4(OutR4), .in5(OutR5), .in6(OutR6), .in7(OutR7),
    .out(ReadData3), .sel(adder_1_out));
  Multiplexer #(.select(3), .width(16)) multiplexer_3 (
    .in0(OutR0), .in1(OutR1), .in2(OutR2), .in3(OutR3), .in4(OutR4), .in5(OutR5), .in6(OutR6), .in7(OutR7),
    .out(RD), .sel(WriteRegister));
  Register #(.width(16)) R0 (.D(WriteData), .en(EN_R0), .clk(Clock), .Q(OutR0));  // open: clr
  Register #(.width(16)) R1 (.D(WriteData), .en(EN_R1), .clk(Clock), .Q(OutR1));  // open: clr
  Register #(.width(16)) R2 (.D(WriteData), .en(EN_R2), .clk(Clock), .Q(OutR2));  // open: clr
  Register #(.width(16)) R3 (.D(WriteData), .en(EN_R3), .clk(Clock), .Q(OutR3));  // open: clr
  Register #(.width(16)) R4 (.D(WriteData), .en(EN_R4), .clk(Clock), .Q(OutR4));  // open: clr
  Register #(.width(16)) R5 (.D(WriteData), .en(EN_R5), .clk(Clock), .Q(OutR5));  // open: clr
  Register #(.width(16)) R6 (.D(WriteData), .en(EN_R6), .clk(Clock), .Q(OutR6));  // open: clr
  Register #(.width(16)) R7 (.D(WriteData), .en(EN_R7), .clk(Clock), .Q(OutR7));  // open: clr
  Multiplexer #(.select(3), .width(16)) multiplexer_4 (
    .in0(OutR0), .in1(OutR1), .in2(OutR2), .in3(OutR3), .in4(OutR4), .in5(OutR5), .in6(OutR6), .in7(OutR7),
    .out(ReadData2), .sel(ReadRegister2));
  Adder #(.width(3)) adder_2 (.a(ReadRegister2), .b(ACC), .out(adder_2_out));  // open: cin, cout
  Multiplexer #(.select(3), .width(16)) multiplexer_5 (
    .in0(OutR0), .in1(OutR1), .in2(OutR2), .in3(OutR3), .in4(OutR4), .in5(OutR5), .in6(OutR6), .in7(OutR7),
    .out(ReadData4), .sel(adder_2_out));

  // Other names for the same wires on the sheet: ACC1[2:0] = ACC; ACC2[2:0] = ACC; ReadRegister3[2:0] = WriteRegister
endmodule
