// Logisim project projeto3_v1_joao.circ as structural Verilog: 4 circuits, main circuit main
module main (
);

  wire clk, OrigAlu, RegWrite;
  wire [1:0] SinalALU;
  wire [2:0] Sel_RD_mais1, Sel_RS1_mais1;
  wire [4:0] Ime_5b;
  wire [10:0] Instrucao;
  wire [15:0] adder_1_out, Dado_RD, Dado_RD_mais1, Dado_RS1, Dado_RS1_mais1, Dado_RS2, Imediato,
       register_1_q, ResultadoALU;

  Clock clock_1 (.out(clk));
  Register #(.width(16)) register_1 (.D(adder_1_out), .clk(clk), .Q(register_1_q));  // open: en, clr
  Adder #(.width(16)) adder_1 (.a(register_1_q), .b(16'h1), .out(adder_1_out));  // open: cin, cout
  ROM #(.addrWidth(16), .dataWidth(16)) rom_1 (.addr(register_1_q), .data({Ime_5b, Instrucao}));
  ControlUnit controlunit_1 (.opcode(Instrucao[1:0]), .SinalAlu(SinalALU), .OrigAlu(OrigAlu), .RegWrite(RegWrite));
  Adder #(.width(3)) adder_2 (.a(Instrucao[4:2]), .b(3'b001), .out(Sel_RD_mais1));  // open: cin, cout
  Adder #(.width(3)) adder_3 (.a(Instrucao[7:5]), .b(3'b001), .out(Sel_RS1_mais1));  // open: cin, cout
  assign Imediato = {{11{Ime_5b[4]}}, Ime_5b};  // Bit_Extender bit_extender_1
  ALU alu_1 (
    .Imediato(Imediato), .Dado_RD(Dado_RD), .Dado_RS1(Dado_RD_mais1), .Dado_RS1_mais1(Dado_RS1),
    .Dado_RD_mais1(Dado_RS1_mais1), .Dado_RS2(Dado_RS2), .SinalALU(SinalALU), .OrigAlu(OrigAlu),
    .Resultado_ALU(ResultadoALU));
  RegisterFile registerfile_1 (
    .RegWrite(RegWrite), .Reg_Destino(Instrucao[4:2]), .Sel_RD(Instrucao[4:2]), .Dados_Escrita(ResultadoALU),
    .clk(clk), .Sel_RS1(Instrucao[7:5]), .Sel_RD_mais1(Sel_RD_mais1), .Sel_RS1_mais1(Sel_RS1_mais1),
    .Sel_RS2(Instrucao[10:8]), .Dado_RD(Dado_RD), .Dado_RS1(Dado_RS1), .Dado_RD_mais1(Dado_RD_mais1),
    .Dado_Rs1_mais1(Dado_RS1_mais1), .Dado_Rs2(Dado_RS2));

  // Other names for the same wires on the sheet: Opcode[1:0] = Instrucao[1:0]; Reg_RD[2:0] = Instrucao[4:2];
  //   Reg_RS1[2:0] = Instrucao[7:5]; Reg_RS2[2:0] = Instrucao[10:8]; Instrucao[15:11] = Ime_5b

  // Notes on the sheet:
  //   contents of rom_1 (hex, n*v repeats v):
  //   1a23 4b56 7c89
endmodule

module ControlUnit (
  input  [1:0] opcode,
  output [1:0] SinalAlu,
  output OrigAlu,
  output RegWrite
);

  and and_1 (OrigAlu, opcode[0], opcode[1]);

  assign RegWrite = 1'b1;
  assign SinalAlu = opcode;
endmodule

module ALU (
  input  [15:0] Imediato,
  input  [15:0] Dado_RD,
  input  [15:0] Dado_RS1,
  input  [15:0] Dado_RS1_mais1,
  input  [15:0] Dado_RD_mais1,
  input  [15:0] Dado_RS2,
  input  [1:0] SinalALU,
  input  OrigAlu,
  output [15:0] Resultado_ALU
);

  wire [15:0] adder_1_out, adder_2_out, adder_3_out, multiplexer_1_out, multiplexer_2_out;

  Adder #(.width(16)) adder_1 (.a(Dado_RD), .b(Dado_RS1), .out(adder_1_out));  // open: cin, cout
  Multiplexer #(.width(16)) multiplexer_1 (.in0(Dado_RD), .in1(Dado_RS1_mais1), .out(multiplexer_1_out), .sel(OrigAlu));
  Multiplexer #(.width(16)) multiplexer_2 (.in0(Dado_RS1), .in1(Dado_RD_mais1), .out(multiplexer_2_out), .sel(OrigAlu));
  Adder #(.width(16)) adder_2 (.a(multiplexer_1_out), .b(multiplexer_2_out), .out(adder_2_out));  // open: cin, cout
  Adder #(.width(16)) adder_3 (.a(adder_2_out), .b(Dado_RD), .out(adder_3_out));  // open: cin, cout
  Multiplexer #(.select(2), .width(16)) multiplexer_3 (
    .in0(Imediato), .in1(adder_1_out), .in2(adder_2_out), .in3(adder_3_out), .out(Resultado_ALU),
    .sel(SinalALU));

  // Notes on the sheet:
  //   add
  //   dot
  //   dota
endmodule

module RegisterFile (
  input  RegWrite,
  input  [2:0] Reg_Destino,
  input  [2:0] Sel_RD,
  input  [15:0] Dados_Escrita,
  input  clk,
  input  [2:0] Sel_RS1,
  input  [2:0] Sel_RD_mais1,
  input  [2:0] Sel_RS1_mais1,
  input  [2:0] Sel_RS2,
  output [15:0] Dado_RD,
  output [15:0] Dado_RS1,
  output [15:0] Dado_RD_mais1,
  output [15:0] Dado_Rs1_mais1,
  output [15:0] Dado_Rs2
);

  wire EN_R0, EN_R1, EN_R2, EN_R3, EN_R4, EN_R5, EN_R6, EN_R7;
  wire [15:0] R0_Out, R1_Out, R2_Out, R3_Out, R4_Out, R5_Out, R6_Out, R7_Out;

  Demultiplexer #(.select(3)) demultiplexer_1 (
    .out0(EN_R0), .out1(EN_R1), .out2(EN_R2), .out3(EN_R3), .out4(EN_R4), .out5(EN_R5), .out6(EN_R6),
    .out7(EN_R7), .in(RegWrite), .sel(Reg_Destino));
  Multiplexer #(.select(3), .width(16)) multiplexer_1 (
    .in0(R0_Out), .in1(R1_Out), .in2(R2_Out), .in3(R3_Out), .in4(R4_Out), .in5(R5_Out), .in6(R6_Out),
    .in7(R7_Out), .out(Dado_RS1), .sel(Sel_RS1));
  Multiplexer #(.select(3), .width(16)) multiplexer_2 (
    .in0(R0_Out), .in1(R1_Out), .in2(R2_Out), .in3(R3_Out), .in4(R4_Out), .in5(R5_Out), .in6(R6_Out),
    .in7(R7_Out), .out(Dado_Rs1_mais1), .sel(Sel_RS1_mais1));
  Multiplexer #(.select(3), .width(16)) multiplexer_3 (
    .in0(R0_Out), .in1(R1_Out), .in2(R2_Out), .in3(R3_Out), .in4(R4_Out), .in5(R5_Out), .in6(R6_Out),
    .in7(R7_Out), .out(Dado_RD), .sel(Sel_RD));
  Multiplexer #(.select(3), .width(16)) multiplexer_4 (
    .in0(R0_Out), .in1(R1_Out), .in2(R2_Out), .in3(R3_Out), .in4(R4_Out), .in5(R5_Out), .in6(R6_Out),
    .in7(R7_Out), .out(Dado_RD_mais1), .sel(Sel_RD_mais1));
  Multiplexer #(.select(3), .width(16)) multiplexer_5 (
    .in0(R0_Out), .in1(R1_Out), .in2(R2_Out), .in3(R3_Out), .in4(R4_Out), .in5(R5_Out), .in6(R6_Out),
    .in7(R7_Out), .out(Dado_Rs2), .sel(Sel_RS2));
  Register #(.width(16)) R0 (.D(Dados_Escrita), .en(EN_R0), .clk(clk), .Q(R0_Out));  // open: clr
  Register #(.width(16)) R1 (.D(Dados_Escrita), .en(EN_R1), .clk(clk), .Q(R1_Out));  // open: clr
  Register #(.width(16)) R2 (.D(Dados_Escrita), .en(EN_R2), .clk(clk), .Q(R2_Out));  // open: clr
  Register #(.width(16)) R3 (.D(Dados_Escrita), .en(EN_R3), .clk(clk), .Q(R3_Out));  // open: clr
  Register #(.width(16)) R4 (.D(Dados_Escrita), .en(EN_R4), .clk(clk), .Q(R4_Out));  // open: clr
  Register #(.width(16)) R5 (.D(Dados_Escrita), .en(EN_R5), .clk(clk));  // open: Q, clr
  Register #(.width(16)) R6 (.D(Dados_Escrita), .en(EN_R6), .clk(clk), .Q(R6_Out));  // open: clr
  Register #(.width(16)) R7 (.D(Dados_Escrita), .en(EN_R7), .clk(clk), .Q(R7_Out));  // open: clr
endmodule
